# Fritzing sketch KTC_ROVER_ARDUINO (saved by Fritzing 0.9.3b)
breadboards: 2

parts:
  Part1 = Arduino Nano (Rev3.0)
  S1 = H-Bridge with L298N
  VCC1 = 4 x AAA Battery Mount
  hc-sr1 = hc-sr04
  D1 = Rectifier Diode [part_number=1N4001 package="300 mil [THT]"]  # not connected
  C1 = Electrolytic Capacitor [capacitance=100µF voltage=50V package="100 mil [THT, electrolytic]"]
  S2 = Pushbutton [package="[THT]"]
  C2 = Ceramic Capacitor [capacitance=100nF package="100 mil [THT, multilayer]"]
  M1 = DC Motor
  M2 = DC Motor

nets:
  GND: Part1.GND, S1.GND, VCC1.-, hc-sr1.GND, C1.-, S2.Pin_3, S2.Pin_4, C2.0
  N1: Part1.D2, S2.Pin_1, S2.Pin_2, C2.1
  N2: Part1.D5, hc-sr1.Trig
  N3: Part1.D6, hc-sr1.Echo
  VIN: Part1.VIN, hc-sr1.VCC, C1.+
  N4: Part1.A3, S1.IN1
  N5: Part1.A2, S1.IN2
  N6: Part1.A1, S1.IN3
  N7: Part1.A0, S1.IN4
  N8: S1.12V, VCC1.+
  N9: S1.M1-01, M1.pin_2
  N10: S1.M1-02, M1.pin_1
  N11: S1.M2-01, M2.pin_2
  N12: S1.M2-02, M2.pin_1

notes:
  TRIG
  ECHO
  VCC
  GND
  1uF
  1000uF

custom parts:
  H-Bridge with L298N: h-bridge
