# Fritzing sketch Single_Motor_Driver (saved by Fritzing 0.9.3b)
breadboards: 1

parts:
  S1 = Pushbutton [package="[THT]"]
  S2 = Pushbutton [package="[THT]"]
  Part1 = Arduino Uno (Rev3)
  VCC1 = Battery
  S3 = H-Bridge with L298N
  M1 = DC Motor

nets:
  N1: S1.Pin_1, S1.Pin_2, Part1.D8
  GND: S1.Pin_3, S1.Pin_4, S2.Pin_3, S2.Pin_4, Part1.GND, VCC1.-, S3.GND
  N2: S2.Pin_1, S2.Pin_2, Part1.D9_PWM
  N3: Part1.A0, S3.IN1
  N4: Part1.A1, S3.IN2
  N5: VCC1.+, S3.12V
  N6: S3.M1-01, M1.pin_2
  N7: S3.M1-02, M1.pin_1

custom parts:
  H-Bridge with L298N: h-bridge
